# Fritzing sketch electronicMaze (saved by Fritzing 0.9.2b)

parts:
  부품1 = Arduino Uno (Rev3)
  부품2 = NeoPixel Stick [part_number=1426]
  U1 = LIPO-1000mAh [package=lipo-1000]
  J1 = Piezo Speaker
  KY-1 = Keyes Relay [package=THT]

nets:
  N1: 부품1.D9_PWM, KY-1.signal
  N2: 부품1.D13/SCK, J1.pin2
  GND: 부품1.GND, 부품2.GND, U1.-, J1.pin1, KY-1.ground
  N3: 부품1.5V, KY-1.power
  N4: 부품2.+5V, KY-1.C
  N5: U1.+, KY-1.NO

custom parts:
  NeoPixel Stick: Make your own little LED strip arrangement with this stick of NeoPixel LEDs. We crammed 8 of the tiny 5050 (5mm x 5mm) smart RGB LEDs onto a PCB with mounting holes and a chainable design. Use only one microcontroller pin to control as many as you can chain together! Each LED is addressable as the driver chip is inside the LED. Each one has ~18mA constant current drive so the color will be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
  Keyes Relay: The Keyes 5V relay module is suitable for SCM development, home appliance control. It uses a 5V~12V TIL control signal which can control DC / AC signal.
